# Fritzing sketch Mini_Estacao_Meteologica_Nano (saved by Fritzing 1.0.1rc)
breadboards: 1

parts:
  DHT1 = DHT11 Humitidy and Temperature Sensor
  Componente2 = GUVA-S12SD UV Light Sensor
  Componente3 = Barometric Pressure Sensor - BMP180 Breakout (GY-68)
  R1 = Resistor [tolerance=±5% resistance=220 package="0402 [SMD]"]
  R2 = Photocell (LDR) [package=THT]
  Componente4 = Bluetooth HC-05 Macho
  R3 = Resistor [tolerance=±5% resistance=10k package="0402 [SMD]"]
  R4 = Resistor [tolerance=±5% resistance=22k package="0402 [SMD]"]
  Componente5 = Arduino Nano (Rev3.0) (ICSP)

nets:
  5V: DHT1.VDD, Componente2.5V, R2.pin_0, Componente4.VCC, Componente5.5V
  N1: DHT1.DATA, Componente5.A2
  GND: DHT1.GND, Componente2.GND, Componente3.GND, R1.Pin_1, Componente4.GND, R4.Pin_1, Componente5.GND
  N2: Componente2.Out, Componente5.A1
  VCC: Componente3.VCC, Componente5.3V3
  N3: Componente3.SCL, Componente5.A5
  N4: Componente3.SDA, Componente5.A4
  N5: R1.Pin_0, R2.pin_1, Componente5.A0
  N6: Componente4.TXD, Componente5.D0/RX
  N7: Componente4.RXD, R3.Pin_1, R4.Pin_0
  N8: R3.Pin_0, Componente5.D1/TX

custom parts:
  DHT11 Humitidy and Temperature Sensor: DHT11 Humidity and Temperature Sensor
  GUVA-S12SD UV Light Sensor: Extend your light-sensing spectrum with this analog UV sensor module. It uses a UV photodiode, which can detect the 240-370nm range of light (which covers UVB and most of UVA spectrum). The signal level from the photodiode is very small, in the nano-ampere level, so we tossed on an opamp to amplify the signal to a more manageable volt-level.
