# Fritzing sketch Mini_Estacao_Relogio_Uno (saved by Fritzing 1.0.1rc)
breadboards: 1

parts:
  Componente1 = Arduino Uno (Rev3) - ICSP
  DHT1 = DHT11 Humitidy and Temperature Sensor
  Componente2 = GUVA-S12SD UV Light Sensor
  Componente3 = Barometric Pressure Sensor - BMP180 Breakout (GY-68)
  R1 = Resistor [tolerance=±5% resistance=220 package="0402 [SMD]"]
  R2 = Photocell (LDR) [package=THT]
  Componente4 = Bluetooth HC-05 Macho
  R3 = Resistor [tolerance=±5% resistance=10k package="0402 [SMD]"]
  R4 = Resistor [tolerance=±5% resistance=22k package="0402 [SMD]"]
  Componente6 = Real Time Clock Module - DS1307 RTC Breakout Board

nets:
  N1: Componente1.A0, R1.Pin_0, R2.pin_1
  N2: Componente1.A1, Componente2.Out
  N3: Componente1.A2, DHT1.DATA
  N4: Componente1.A4/SDA, Componente3.SDA, Componente6.SDA
  N5: Componente1.A5/SCL, Componente3.SCL, Componente6.SCL
  GND: Componente1.GND, DHT1.GND, Componente2.GND, Componente3.GND, R1.Pin_1, Componente4.GND, R4.Pin_1, Componente6.GND
  N6: Componente1.D0/RX, Componente4.TXD
  N7: Componente1.D1/TX, R3.Pin_0
  N8: Componente1.IOREF, Componente4.VCC
  3V3: Componente1.3V3, Componente3.VCC
  5V: Componente1.5V, DHT1.VDD, Componente2.5V, R2.pin_0, Componente6.5V
  N9: Componente4.RXD, R3.Pin_1, R4.Pin_0

custom parts:
  DHT11 Humitidy and Temperature Sensor: DHT11 Humidity and Temperature Sensor
  GUVA-S12SD UV Light Sensor: Extend your light-sensing spectrum with this analog UV sensor module. It uses a UV photodiode, which can detect the 240-370nm range of light (which covers UVB and most of UVA spectrum). The signal level from the photodiode is very small, in the nano-ampere level, so we tossed on an opamp to amplify the signal to a more manageable volt-level.
